// Logisim project Computer.circ as structural Verilog: 5 circuits, main circuit Test Field
// ACC
module Test_Field (
  input  [11:0] in_1,
  input  Breakpoint_Enable
);

  wire AC_0, AC_15, ACC_CLR, ACC_INC, ACC_LD, ADD, AND, AR_CLR, AR_INC, AR_LD, Breakpoint, button_2_out,
       Carry_Overflow, CLK, clock_1_out, comparator_1_eq, DR_INC, DR_LD, DR_PASS, E, e_control_1_d,
       e_control_1_e_prime, E_prime, E_RESET, E_SET, FGI, FGI_RESET, FGI_SET, FGO, FGO_RESET, FGO_SET, I,
       I_O_REGISTER_RESET, I_RESET, I_SET, IEN, IEN_RESET, IEN_SET, INPR, IR_LD, Master_CLK, MEMORY_READ,
       MEMORY_WRITE, NOT, not_1_out, or_1_out, or_2_out, or_3_out, OUTR_LD, PC_CLR, PC_INC, PC_LD, R,
       R_RESET, R_SET, S, S0, S1, S2, S__En, S_RESET, SC_RESET, SHL, SHR, TR_LD;
  wire [3:0] SC;
  wire [6:0] Input, Input_Register, OUT;
  wire [15:0] Accumulator, Address_Register, BUS, Data_Register, Instuction_Register, MEMORY,
       Program_Counter, Temporary_Register;
  wire [31:0] counter_2_q;

  D_Flip_Flop d_ff_1 (.Q(S__En), .preset(S), .reset(or_1_out));  // open: clk, D, Qn, en
  or or_1 (or_1_out, S_RESET, Breakpoint);
  D_Flip_Flop u_I (.Q(I), .preset(I_SET), .reset(I_RESET));  // open: clk, D, Qn, en
  Counter #(.width(4), .max('hf)) counter_1 (.Q(SC), .clk(Master_CLK), .clr(SC_RESET));  // open: load, D, count, carry
  and u_S (Master_CLK, CLK, S__En);
  _16_Bit_Counter_w__Parallel_Load u_Address_Register (
    .INP(BUS), .LD(AR_LD), .INC(AR_INC), .DEC(1'b0), .CLK(Master_CLK), .CLR(AR_CLR), .Q(Address_Register));
  _16_Bit_Counter_w__Parallel_Load Instruction_Register (
    .INP(BUS), .LD(IR_LD), .INC(1'b0), .DEC(1'b0), .CLK(Master_CLK), .CLR(1'b0), .Q(Instuction_Register));
  D_Flip_Flop u_IEN (.Q(IEN), .preset(IEN_SET), .reset(IEN_RESET));  // open: clk, D, Qn, en
  _16_Bit_ALU u_16_bit_alu_1 (
    .Data_Register(Data_Register), .ACC_CLR(ACC_CLR), .Accumulator(Accumulator), .CLK(Master_CLK),
    .ACC_LD(ACC_LD), .ADD(ADD), .AND(AND), .NOT(NOT), .DR_Pass(DR_PASS), .SHR(SHR), .SHL(SHL),
    .ACC_INC(ACC_INC), .Input_Register(Input_Register), .INPR(INPR), .E(E), .AC__0(AC_0), .AC__15(AC_15),
    .IC__15(Carry_Overflow));
  D_Flip_Flop u_R (.Q(R), .preset(R_SET), .reset(R_RESET));  // open: clk, D, Qn, en
  Control_Unit control_unit_1 (
    .IR(Instuction_Register), .R(R), .I(I), .E(E), .IEN(IEN), .FGI(FGI), .FGO(FGO), .DR(Data_Register),
    .ACC(Accumulator), .AR__LD(AR_LD), .AR__INR(AR_INC), .PC__LD(PC_LD), .AR__CLR(AR_CLR), .PC__INR(PC_INC),
    .PC__CLR(PC_CLR), .SC(SC), .ACC__LD(ACC_LD), .ACC__INR(ACC_INC), .ACC__CLR(ACC_CLR), .OUTR__LD(OUTR_LD),
    .DR__LD(DR_LD), .DR__INR(DR_INC), .IR__LD(IR_LD), .TR__LD(TR_LD), .IEN__SET(IEN_SET),
    .IEN__RESET(IEN_RESET), .R__SET(R_SET), .R__RESET(R_RESET), .FGI__RESET(FGI_RESET),
    .FGO__RESET(FGO_RESET), .SC__RESET(SC_RESET), .I__SET(I_SET), .I__RESET(I_RESET), .E__SET(E_SET),
    .E__RESET(E_RESET), .Memory__READ(MEMORY_READ), .S__RESET(S_RESET), .Memory__WRITE(MEMORY_WRITE),
    .S0(S0), .S1(S1), .S3(S2), .AND(AND), .ADD(ADD), .DR_PASS(DR_PASS), .NOT(NOT), .SHR(SHR), .SHL(SHL),
    .INPR(INPR), .E_prime(E_prime), .FGO__SET(FGO_SET));
  D_Flip_Flop u_FGI (.Q(FGI), .preset(FGI_SET), .reset(FGI_RESET));  // open: clk, D, Qn, en
  Register #(.width(7)) u_Input_Register (
    .D(Input), .en(FGI_SET), .Q(Input_Register), .clk(Master_CLK), .clr(or_2_out));
  _16_Bit_Counter_w__Parallel_Load u_Program_Counter (
    .INP(BUS), .LD(PC_LD), .INC(PC_INC), .DEC(1'b0), .CLK(Master_CLK), .CLR(PC_CLR), .Q(Program_Counter));
  _16_Bit_Counter_w__Parallel_Load u_Temporary_Register (
    .INP(BUS), .LD(TR_LD), .INC(1'b0), .DEC(1'b0), .CLK(Master_CLK), .CLR(1'b0), .Q(Temporary_Register));
  or or_2 (or_2_out, I_O_REGISTER_RESET, MEMORY_WRITE);
  or or_3 (or_3_out, OUT[0], OUT[1], OUT[2], OUT[3], OUT[4], OUT[5], OUT[6]);
  D_Flip_Flop u_FGO (.Q(FGO), .preset(FGO_SET), .reset(FGO_RESET));  // open: clk, D, Qn, en
  and and_1 (I_O_REGISTER_RESET, or_3_out, FGO_SET);
  Multiplexer #(.select(3), .width(16)) multiplexer_1 (
    .in1(Address_Register), .in2(Program_Counter), .in3(Data_Register), .in4(Accumulator),
    .in5(Instuction_Register), .in6(Temporary_Register), .in7(MEMORY), .out(BUS), .sel({S2, S1, S0}));  // open: in0, en
  _16_Bit_Counter_w__Parallel_Load u_Data_Register (
    .INP(BUS), .LD(DR_LD), .INC(DR_INC), .DEC(1'b0), .CLK(Master_CLK), .CLR(1'b0), .Q(Data_Register));
  Register #(.width(7)) Output_Register (
    .D(BUS[6:0]), .en(OUTR_LD), .Q(OUT), .clk(Master_CLK), .clr(I_O_REGISTER_RESET));
  E_CONTROL e_control_1 (
    .D(e_control_1_d), .ADD(ADD), .AC_15(AC_15), .SHL(SHL), .AC_0(AC_0), .SHR(SHR),
    .CARRY_OVERFLOW(Carry_Overflow), .CU_E_prime(E_prime), .E_prime(e_control_1_e_prime));
  J_K_Flip_Flop u_E (
    .J(e_control_1_d), .clk(Master_CLK), .K(e_control_1_e_prime), .Q(E), .en(E_SET), .reset(E_RESET));  // open: Qn, preset
  or or_4 (CLK, clock_1_out, button_2_out);
  Button button_1 (.out(S));
  // Probe on Address_Register[11:0]
  // Probe on Address_Register[14:12]
  Clock clock_1 (.out(clock_1_out));
  Button button_2 (.out(button_2_out));
  // Probe on MEMORY
  // Probe on Program_Counter
  // Probe on Data_Register
  // Probe on Accumulator
  // Probe on Instuction_Register
  // Probe on Temporary_Register
  // Probe on BUS
  // Probe on SC
  LED led_1 (.in(S__En));
  Keyboard keyboard_1 (.clk(Master_CLK), .re(1'b1), .clr(FGI_RESET), .avail(FGI_SET), .data(Input));
  TTY tty_1 (.data(OUT), .clk(Master_CLK), .we(not_1_out));  // open: clr
  not not_1 (not_1_out, FGO);
  Comparator #(.width(12)) comparator_1 (.a(Address_Register[11:0]), .b(in_1), .eq(comparator_1_eq));  // open: gt, lt
  LED led_2 (.in(E));
  LED led_3 (.in(I));
  LED led_4 (.in(IEN));
  LED led_5 (.in(R));
  LED led_6 (.in(FGI));
  LED led_7 (.in(FGO));
  and and_2 (Breakpoint, comparator_1_eq, Breakpoint_Enable);
  RAM #(.addrWidth(12), .dataWidth(16), .bus("separate")) ram_1 (
    .addr(Address_Register[11:0]), .din(BUS), .data(MEMORY), .str(MEMORY_WRITE), .sel(1'b1),
    .clk(Master_CLK), .ld(MEMORY_READ));  // open: clr
  Counter #(.width(32), .max('hffffffff)) counter_2 (
    .Q(counter_2_q), .clk(Master_CLK));  // open: load, D, count, carry, clr
  // Probe on counter_2_q

  // Other names for the same wires on the sheet: AR[11:0] = Address_Register[11:0]

  // Notes on the sheet:
  //   Control Panel
  //   Memory
endmodule

module ALU_ACC_Cell (
  input  ADD,
  input  Carry_Overflow_i_1,
  input  LD,
  input  DR_i,
  input  AND,
  input  CLK,
  input  CLR,
  input  NOT,
  input  DR,
  input  SHR,
  input  AC_i_1,
  input  SHL,
  input  AC_i_1_2,
  input  IC,
  input  INC,
  input  INPR,
  input  INPR_i,
  output AC_i,
  output E,
  output ICO
);

  wire AC_i____DR_i_out, AC_i__prime_out, adder_1_out, adder_2_out, and_1_out, and_2_out, DR_i____AC_i_out,
       DR_i_out, INC_out, INPR_i_out, not_1_out, not_2_out, or_1_out, SHL_out, SHR_out;

  Adder #(.width(1)) adder_1 (.a(AC_i), .b(DR_i), .out(adder_1_out), .cin(Carry_Overflow_i_1), .cout(E));
  Adder #(.width(1)) adder_2 (.a(AC_i), .b(IC), .out(adder_2_out), .cin(1'b0), .cout(ICO));
  and DR_i____AC_i (DR_i____AC_i_out, ADD, adder_1_out);
  and AC_i____DR_i (AC_i____DR_i_out, AND, AC_i, DR_i);
  and AC_i__prime (AC_i__prime_out, NOT, not_1_out);
  not not_1 (not_1_out, AC_i);
  and u_DR_i (DR_i_out, DR, DR_i);
  and u_SHR (SHR_out, SHR, AC_i_1);
  and u_SHL (SHL_out, SHL, AC_i_1_2);
  and u_INC (INC_out, adder_2_out, INC);
  and u_INPR_i (INPR_i_out, INPR, INPR_i);
  or or_1 (or_1_out, DR_i____AC_i_out, AC_i____DR_i_out, AC_i__prime_out, DR_i_out, SHR_out, SHL_out, INC_out, INPR_i_out);
  and and_1 (and_1_out, LD, or_1_out);
  and and_2 (and_2_out, LD, not_2_out);
  not not_2 (not_2_out, or_1_out);
  J_K_Flip_Flop u_AC_i (.J(and_1_out), .clk(CLK), .K(and_2_out), .Q(AC_i), .reset(CLR));  // open: Qn, preset, en
endmodule

module _16_Bit_ALU (
  input  ACC_LD,
  input  ADD,
  input  AND,
  input  NOT,
  input  DR_Pass,
  input  SHR,
  input  SHL,
  input  INPR,
  input  ACC_INC,
  input  [15:0] Data_Register,
  input  CLK,
  input  ACC_CLR,
  input  E,
  input  [6:0] Input_Register,
  output [15:0] Accumulator,
  output AC__0,
  output AC__15,
  output IC__15
);

  wire E0, E1, E2, E3, E4, E5, E6, E7, E8, E9, E10, E11, E12, E13, E14, E15, IC_0, IC_1, IC_2, IC_3, IC_4,
       IC_5, IC_6, IC_7, IC_8, IC_9, IC_10, IC_11, IC_12, IC_13, IC_14;

  ALU_ACC_Cell alu_acc_cell_1 (
    .DR_i(Data_Register[0]), .NOT(NOT), .DR(DR_Pass), .AC_i(AC__0), .Carry_Overflow_i_1(1'b0), .ADD(ADD),
    .AND(AND), .LD(ACC_LD), .CLK(CLK), .E(E0), .SHR(SHR), .SHL(SHL), .AC_i_1(Accumulator[1]), .AC_i_1_2(E),
    .CLR(ACC_CLR), .IC(1'b1), .INC(ACC_INC), .ICO(IC_0), .INPR(INPR), .INPR_i(Input_Register[0]));
  ALU_ACC_Cell alu_acc_cell_2 (
    .DR_i(Data_Register[1]), .NOT(NOT), .DR(DR_Pass), .AC_i(Accumulator[1]), .Carry_Overflow_i_1(E0),
    .ADD(ADD), .AND(AND), .LD(ACC_LD), .CLK(CLK), .E(E1), .SHR(SHR), .SHL(SHL), .AC_i_1(Accumulator[2]),
    .AC_i_1_2(AC__0), .CLR(ACC_CLR), .IC(IC_0), .INC(ACC_INC), .ICO(IC_1), .INPR(INPR),
    .INPR_i(Input_Register[1]));
  ALU_ACC_Cell alu_acc_cell_3 (
    .DR_i(Data_Register[2]), .NOT(NOT), .DR(DR_Pass), .AC_i(Accumulator[2]), .Carry_Overflow_i_1(E1),
    .ADD(ADD), .AND(AND), .LD(ACC_LD), .CLK(CLK), .E(E2), .SHR(SHR), .SHL(SHL), .AC_i_1(Accumulator[3]),
    .AC_i_1_2(Accumulator[1]), .CLR(ACC_CLR), .IC(IC_1), .INC(ACC_INC), .ICO(IC_2), .INPR(INPR),
    .INPR_i(Input_Register[2]));
  ALU_ACC_Cell alu_acc_cell_4 (
    .DR_i(Data_Register[3]), .NOT(NOT), .DR(DR_Pass), .AC_i(Accumulator[3]), .Carry_Overflow_i_1(E2),
    .ADD(ADD), .AND(AND), .LD(ACC_LD), .CLK(CLK), .E(E3), .SHR(SHR), .SHL(SHL), .AC_i_1(Accumulator[4]),
    .AC_i_1_2(Accumulator[2]), .CLR(ACC_CLR), .IC(IC_2), .INC(ACC_INC), .ICO(IC_3), .INPR(INPR),
    .INPR_i(Input_Register[3]));
  ALU_ACC_Cell alu_acc_cell_5 (
    .DR_i(Data_Register[4]), .NOT(NOT), .DR(DR_Pass), .AC_i(Accumulator[4]), .Carry_Overflow_i_1(E3),
    .ADD(ADD), .AND(AND), .LD(ACC_LD), .CLK(CLK), .E(E4), .SHR(SHR), .SHL(SHL), .AC_i_1(Accumulator[5]),
    .AC_i_1_2(Accumulator[3]), .CLR(ACC_CLR), .IC(IC_3), .INC(ACC_INC), .ICO(IC_4), .INPR(INPR),
    .INPR_i(Input_Register[4]));
  ALU_ACC_Cell alu_acc_cell_6 (
    .DR_i(Data_Register[5]), .NOT(NOT), .DR(DR_Pass), .AC_i(Accumulator[5]), .Carry_Overflow_i_1(E4),
    .ADD(ADD), .AND(AND), .LD(ACC_LD), .CLK(CLK), .E(E5), .SHR(SHR), .SHL(SHL), .AC_i_1(Accumulator[6]),
    .AC_i_1_2(Accumulator[4]), .CLR(ACC_CLR), .IC(IC_4), .INC(ACC_INC), .ICO(IC_5), .INPR(INPR),
    .INPR_i(Input_Register[5]));
  ALU_ACC_Cell alu_acc_cell_7 (
    .DR_i(Data_Register[6]), .NOT(NOT), .DR(DR_Pass), .AC_i(Accumulator[6]), .Carry_Overflow_i_1(E5),
    .ADD(ADD), .AND(AND), .LD(ACC_LD), .CLK(CLK), .E(E6), .SHR(SHR), .SHL(SHL), .AC_i_1(Accumulator[7]),
    .AC_i_1_2(Accumulator[5]), .CLR(ACC_CLR), .IC(IC_5), .INC(ACC_INC), .ICO(IC_6), .INPR(INPR),
    .INPR_i(Input_Register[6]));
  ALU_ACC_Cell alu_acc_cell_8 (
    .DR_i(Data_Register[7]), .NOT(NOT), .DR(DR_Pass), .AC_i(Accumulator[7]), .Carry_Overflow_i_1(E6),
    .ADD(ADD), .AND(AND), .LD(ACC_LD), .CLK(CLK), .E(E7), .SHR(SHR), .SHL(SHL), .AC_i_1(Accumulator[8]),
    .AC_i_1_2(Accumulator[6]), .CLR(ACC_CLR), .IC(IC_6), .INC(ACC_INC), .ICO(IC_7), .INPR(INPR), .INPR_i(1'b0));
  ALU_ACC_Cell alu_acc_cell_9 (
    .DR_i(Data_Register[8]), .NOT(NOT), .DR(DR_Pass), .AC_i(Accumulator[8]), .Carry_Overflow_i_1(E7),
    .ADD(ADD), .AND(AND), .LD(ACC_LD), .CLK(CLK), .E(E8), .SHR(SHR), .SHL(SHL), .AC_i_1(Accumulator[9]),
    .AC_i_1_2(Accumulator[7]), .CLR(ACC_CLR), .IC(IC_7), .INC(ACC_INC), .ICO(IC_8), .INPR(INPR), .INPR_i(1'b0));
  ALU_ACC_Cell alu_acc_cell_10 (
    .DR_i(Data_Register[9]), .NOT(NOT), .DR(DR_Pass), .AC_i(Accumulator[9]), .Carry_Overflow_i_1(E8),
    .ADD(ADD), .AND(AND), .LD(ACC_LD), .CLK(CLK), .E(E9), .SHR(SHR), .SHL(SHL), .AC_i_1(Accumulator[10]),
    .AC_i_1_2(Accumulator[8]), .CLR(ACC_CLR), .IC(IC_8), .INC(ACC_INC), .ICO(IC_9), .INPR(INPR), .INPR_i(1'b0));
  ALU_ACC_Cell alu_acc_cell_11 (
    .DR_i(Data_Register[10]), .NOT(NOT), .DR(DR_Pass), .AC_i(Accumulator[10]), .Carry_Overflow_i_1(E9),
    .ADD(ADD), .AND(AND), .LD(ACC_LD), .CLK(CLK), .E(E10), .SHR(SHR), .SHL(SHL), .AC_i_1(Accumulator[11]),
    .AC_i_1_2(Accumulator[9]), .CLR(ACC_CLR), .IC(IC_9), .INC(ACC_INC), .ICO(IC_10), .INPR(INPR),
    .INPR_i(1'b0));
  ALU_ACC_Cell alu_acc_cell_12 (
    .DR_i(Data_Register[11]), .NOT(NOT), .DR(DR_Pass), .AC_i(Accumulator[11]), .Carry_Overflow_i_1(E10),
    .ADD(ADD), .AND(AND), .LD(ACC_LD), .CLK(CLK), .E(E11), .SHR(SHR), .SHL(SHL), .AC_i_1(Accumulator[12]),
    .AC_i_1_2(Accumulator[10]), .CLR(ACC_CLR), .IC(IC_10), .INC(ACC_INC), .ICO(IC_11), .INPR(INPR),
    .INPR_i(1'b0));
  ALU_ACC_Cell alu_acc_cell_13 (
    .DR_i(Data_Register[12]), .NOT(NOT), .DR(DR_Pass), .AC_i(Accumulator[12]), .Carry_Overflow_i_1(E11),
    .ADD(ADD), .AND(AND), .LD(ACC_LD), .CLK(CLK), .E(E12), .SHR(SHR), .SHL(SHL), .AC_i_1(Accumulator[13]),
    .AC_i_1_2(Accumulator[11]), .CLR(ACC_CLR), .IC(IC_11), .INC(ACC_INC), .ICO(IC_12), .INPR(INPR),
    .INPR_i(1'b0));
  ALU_ACC_Cell alu_acc_cell_14 (
    .DR_i(Data_Register[13]), .NOT(NOT), .DR(DR_Pass), .AC_i(Accumulator[13]), .Carry_Overflow_i_1(E12),
    .ADD(ADD), .AND(AND), .LD(ACC_LD), .CLK(CLK), .E(E13), .SHR(SHR), .SHL(SHL), .AC_i_1(Accumulator[14]),
    .AC_i_1_2(Accumulator[12]), .CLR(ACC_CLR), .IC(IC_12), .INC(ACC_INC), .ICO(IC_13), .INPR(INPR),
    .INPR_i(1'b0));
  ALU_ACC_Cell alu_acc_cell_15 (
    .DR_i(Data_Register[14]), .NOT(NOT), .DR(DR_Pass), .AC_i(Accumulator[14]), .Carry_Overflow_i_1(E13),
    .ADD(ADD), .AND(AND), .LD(ACC_LD), .CLK(CLK), .E(E14), .SHR(SHR), .SHL(SHL), .AC_i_1(AC__15),
    .AC_i_1_2(Accumulator[13]), .CLR(ACC_CLR), .IC(IC_13), .INC(ACC_INC), .ICO(IC_14), .INPR(INPR),
    .INPR_i(1'b0));
  ALU_ACC_Cell alu_acc_cell_16 (
    .DR_i(Data_Register[15]), .NOT(NOT), .DR(DR_Pass), .AC_i(AC__15), .Carry_Overflow_i_1(E14), .ADD(ADD),
    .AND(AND), .LD(ACC_LD), .CLK(CLK), .E(E15), .SHR(SHR), .SHL(SHL), .AC_i_1(E), .AC_i_1_2(Accumulator[14]),
    .CLR(ACC_CLR), .IC(IC_14), .INC(ACC_INC), .ICO(IC__15), .INPR(INPR), .INPR_i(1'b0));

  assign {Accumulator[15], Accumulator[0]} = {AC__15, AC__0};

  // Other names for the same wires on the sheet: AC_0 = AC__0; AC_1 = Accumulator[1]; AC_2 = Accumulator[2];
  //   AC_3 = Accumulator[3]; AC_4 = Accumulator[4]; AC_5 = Accumulator[5]; AC_6 = Accumulator[6];
  //   AC_7 = Accumulator[7]; AC_8 = Accumulator[8]; AC_9 = Accumulator[9]; AC_10 = Accumulator[10];
  //   AC_11 = Accumulator[11]; AC_12 = Accumulator[12]; AC_13 = Accumulator[13]; AC_14 = Accumulator[14];
  //   AC_15 = AC__15; Control_Unit[7:0] = {ACC_INC, ACC_LD, ADD, AND, NOT, DR_Pass, SHR, SHL}; IC_15 = IC__15;
  //   INPR_0 = Input_Register[0]; INPR_1 = Input_Register[1]; INPR_2 = Input_Register[2]; INPR_3 = Input_Register[3];
  //   INPR_4 = Input_Register[4]; INPR_5 = Input_Register[5]; INPR_6 = Input_Register[6]
endmodule

module _16_Bit_Counter_w__Parallel_Load (
  input  [15:0] INP,
  input  LD,
  input  INC,
  input  DEC,
  input  CLK,
  input  CLR,
  output [15:0] Q
);

  wire and_1_out, and_2_out, not_1_out, not_2_out, or_1_out, or_2_out;

  or or_1 (or_1_out, LD, DEC);
  or or_2 (or_2_out, INC, DEC);
  not not_1 (not_1_out, INC);
  not not_2 (not_2_out, LD);
  and and_1 (and_1_out, or_1_out, not_1_out);
  and and_2 (and_2_out, or_2_out, not_2_out);
  Counter #(.width(16), .max('hffff)) counter_1 (
    .load(and_1_out), .D(INP), .count(and_2_out), .Q(Q), .clk(CLK), .clr(CLR));  // open: carry
endmodule

module E_CONTROL (
  input  CU_E_prime,
  input  CARRY_OVERFLOW,
  input  ADD,
  input  SHL,
  input  AC_15,
  input  AC_0,
  input  SHR,
  output E_prime,
  output D
);

  wire and_1_out, and_2_out, and_4_out, or_1_out;

  and and_1 (and_1_out, AC_15, SHL);
  and and_2 (and_2_out, ADD, AC_15);
  or or_1 (or_1_out, and_2_out, and_1_out, and_4_out, CARRY_OVERFLOW);
  and and_3 (E_prime, D, CU_E_prime);
  Multiplexer multiplexer_1 (.in0(or_1_out), .in1(CU_E_prime), .out(D), .sel(CU_E_prime));  // open: en
  and and_4 (and_4_out, AC_0, SHR);
endmodule
