// Logisim project Control Unit.circ as structural Verilog: 20 circuits, main circuit Control Unit
module TEST_SPACE (
  input  [15:0] IR,
  input  [15:0] DR,
  input  [15:0] AC,
  input  IEN,
  input  R,
  input  FGI,
  input  FGO,
  input  I,
  input  E,
  input  CLK,
  output SHL,
  output SHR,
  output NOT,
  output DR_PASS,
  output ADD,
  output AND,
  output S0,
  output S1,
  output S2,
  output MEMORY_READ,
  output MEMORY_WRITE,
  output AR_LD,
  output AR_INR,
  output AR_CLR,
  output PC_LD,
  output PC_INR,
  output PC_CLR,
  output DR_LD,
  output DR_INR,
  output AC_LD,
  output AC_INR,
  output AC_CLR,
  output IR_LD,
  output TR_LD,
  output OUTR_LD,
  output FGI_2,
  output IEN__S,
  output E__S,
  output FGO_2,
  output IEN__R,
  output E__R,
  output I__S,
  output S,
  output R__S,
  output I__R,
  output R__R,
  output SC
);

  wire D0, D1, D2, D3, D4, D5, D6, D7, d_ff_1_qn, d_ff_2_qn, d_ff_3_qn, d_ff_4_qn, d_ff_5_qn, d_ff_6_qn,
       d_ff_7_qn, d_ff_8_qn, or_1_out;
  wire [3:0] counter_1_q;

  Decoder #(.select(3)) decoder_1 (
    .out0(D0), .out1(D1), .out2(D2), .out3(D3), .out4(D4), .out5(D5), .out6(D6), .out7(D7), .sel(IR[14:12]));  // open: en
  D_Flip_Flop d_ff_1 (.clk(AND), .D(d_ff_1_qn), .Qn(d_ff_1_qn));  // open: Q, preset, en, reset
  D_Flip_Flop d_ff_2 (.clk(SHR), .D(d_ff_2_qn), .Qn(d_ff_2_qn));  // open: Q, preset, en, reset
  D_Flip_Flop d_ff_3 (.clk(ADD), .D(d_ff_3_qn), .Qn(d_ff_3_qn));  // open: Q, preset, en, reset
  D_Flip_Flop d_ff_4 (.clk(SHL), .D(d_ff_4_qn), .Qn(d_ff_4_qn));  // open: Q, preset, en, reset
  D_Flip_Flop d_ff_5 (.clk(DR_PASS), .D(d_ff_5_qn), .Qn(d_ff_5_qn));  // open: Q, preset, en, reset
  D_Flip_Flop d_ff_6 (.clk(AC_INR), .D(d_ff_6_qn), .Qn(d_ff_6_qn));  // open: Q, preset, en, reset
  D_Flip_Flop d_ff_7 (.clk(NOT), .D(d_ff_7_qn), .Qn(d_ff_7_qn));  // open: Q, preset, en, reset
  Counter #(.width(4), .max('hf)) counter_1 (.Q(counter_1_q), .clk(CLK), .clr(SC));  // open: load, D, count, carry
  Control_Unit control_unit_1 (
    .IR(IR), .R(R), .I(I), .E(E), .IEN(IEN), .FGI(FGI), .FGO(FGO), .DR(DR), .ACC(AC), .AR__LD(AR_LD),
    .AR__INR(AR_INR), .PC__LD(PC_LD), .AR__CLR(AR_CLR), .PC__INR(PC_INR), .PC__CLR(PC_CLR), .SC(counter_1_q),
    .ACC__LD(AC_LD), .ACC__INR(AC_INR), .ACC__CLR(AC_CLR), .OUTR__LD(OUTR_LD), .DR__LD(DR_LD),
    .DR__INR(DR_INR), .IR__LD(IR_LD), .TR__LD(TR_LD), .IEN__SET(IEN__S), .IEN__RESET(IEN__R), .R__SET(R__S),
    .R__RESET(R__R), .FGI__RESET(FGI_2), .FGO__RESET(FGO_2), .SC__RESET(SC), .I__SET(I__S), .I__RESET(I__R),
    .E__SET(E__S), .E__RESET(E__R), .Memory__READ(MEMORY_READ), .S__RESET(S), .Memory__WRITE(MEMORY_WRITE),
    .S0(S0), .S1(S1), .S3(S2), .AND(AND), .ADD(ADD), .DR_PASS(DR_PASS), .NOT(NOT), .SHR(SHR), .SHL(SHL));  // open: INPR, E_prime, FGO__SET
  // Probe on {S2, S1, S0}
  or or_1 (or_1_out, S2, S1, S0);
  D_Flip_Flop d_ff_8 (.clk(or_1_out), .D(d_ff_8_qn), .Qn(d_ff_8_qn));  // open: Q, preset, en, reset

  // Other names for the same wires on the sheet: INC = AC_INR
endmodule

module Control_Unit (
  input  [3:0] SC,
  input  [15:0] IR,
  input  R,
  input  I,
  input  E,
  input  IEN,
  input  FGI,
  input  FGO,
  input  [15:0] DR,
  input  [15:0] ACC,
  output AR__LD,
  output AR__INR,
  output PC__LD,
  output AR__CLR,
  output PC__INR,
  output PC__CLR,
  output ACC__LD,
  output ACC__INR,
  output ACC__CLR,
  output OUTR__LD,
  output DR__LD,
  output DR__INR,
  output IR__LD,
  output TR__LD,
  output IEN__SET,
  output IEN__RESET,
  output R__SET,
  output R__RESET,
  output FGI__RESET,
  output FGO__RESET,
  output FGO__SET,
  output SC__RESET,
  output I__SET,
  output I__RESET,
  output E__SET,
  output E__RESET,
  output Memory__READ,
  output S__RESET,
  output Memory__WRITE,
  output S0,
  output S1,
  output NOT,
  output AND,
  output S3,
  output SHR,
  output ADD,
  output SHL,
  output DR_PASS,
  output INPR,
  output E_prime
);

  wire D0, D1, D2, D3, D4, D5, D6, D7, not_1_out, not_2_out, not_3_out, p, p_NEW, p_NEW_2, r_NEW, r_t,
       r_TEST, T0, T1, T2, T3, T4, T5, T6, T7, T8, T9, T10, T11, T12, T13, T14, T15;

  not not_1 (not_1_out, I);
  not not_2 (not_2_out, I);
  Decoder #(.select(4)) decoder_1 (
    .out0(T0), .out1(T1), .out2(T2), .out3(T3), .out4(T4), .out5(T5), .out6(T6), .out7(T7), .out8(T8),
    .out9(T9), .out10(T10), .out11(T11), .out12(T12), .out13(T13), .out14(T14), .out15(T15), .sel(SC));  // open: en
  Decoder #(.select(3)) decoder_2 (
    .out0(D0), .out1(D1), .out2(D2), .out3(D3), .out4(D4), .out5(D5), .out6(D6), .out7(D7), .sel(IR[14:12]));  // open: en
  and and_1 (r_NEW, D7, not_1_out, T4);
  and and_2 (p_NEW, D7, I, T4);
  and and_3 (r_TEST, D7, not_2_out, T2);
  and and_4 (p_NEW_2, D7, I, T5);
  not not_3 (not_3_out, I);
  and and_5 (r_t, D7, not_3_out, T3);
  and and_6 (p, D7, I, T3);
  IEN ien_1 (.B7(IR[7]), .p(p), .B6(IR[6]), .R(R), .T2(T2), .SET(IEN__SET), .RESET(IEN__RESET));
  FGI fgi_1 (.p(p), .B11(IR[11]), .RESET(FGI__RESET));
  FGO fgo_1 (.p(p), .B10(IR[10]), .RESET(FGO__RESET), .T0(T0), .SET(FGO__SET));
  I i_1 (.R(R), .T2(T2), .IR_15(IR[15]), .SET(I__SET), .RESET(I__RESET));
  E e_1 (.r(r_t), .B10(IR[10]), .SET(E__SET), .RESET(E__RESET), .B6(IR[6]), .B7(IR[7]), .B8(IR[8]));
  S s_1 (.r(r_t), .B0(IR[0]), .RESET(S__RESET));
  and and_7 (E_prime, IR[8], r_t);
  AR ar_1 (
    .T0(T0), .T2(T2), .R(R), .T3(T3), .D7(D7), .I(I), .T4(T4), .D5(D5), .LD(AR__LD), .INR(AR__INR),
    .CLR(AR__CLR));
  ACC acc_1 (
    .T5(T5), .D0(D0), .D1(D1), .D2(D2), .r(r_t), .B6(IR[6]), .B7(IR[7]), .B9(IR[9]), .B11(IR[11]), .p(p),
    .B5(IR[5]), .LD(ACC__LD), .INR(ACC__INR), .CLR(ACC__CLR));
  DR dr_1 (.T4(T4), .D0(D0), .D1(D1), .D2(D2), .D6(D6), .T5(T5), .LD(DR__LD), .INR(DR__INR));
  BUS_CONTROL bus_control_1 (
    .T4(T4), .D4(D4), .T5(T5), .D5(D5), .T0(T0), .D6(D6), .T6(T6), .D3(D3), .p(p), .B10(IR[10]), .R(R),
    .T2(T2), .T1(T1), .MEMORY__READ(Memory__READ), .S0(S0), .S1(S1), .S2(S3));
  OUTR outr_1 (.p(p), .B10(IR[10]), .LD(OUTR__LD));
  IR ir_1 (.R(R), .T1(T1), .LD(IR__LD));
  TR tr_1 (.R(R), .T0(T0), .LD(TR__LD));
  R r_1 (.IEN(IEN), .FGI(FGI), .FGO(FGO), .R(R), .T2(T2), .SET(R__SET), .RESET(R__RESET), .T1(T1), .T0(T0), .T3(T3));
  and and_8 (NOT, r_t, IR[9]);
  and and_9 (SHR, r_t, IR[7]);
  and and_10 (SHL, r_t, IR[6]);
  and and_11 (INPR, IR[11], p);
  SC sc_1 (
    .T3(T3), .R(R), .T5(T5), .D3(D3), .D4(D4), .T6(T6), .D0(D0), .D1(D1), .D2(D2), .D5(D5), .T7(T7), .D6(D6),
    .r_NEW(r_NEW), .p_NEW(p_NEW_2), .CLR(SC__RESET));
  MEMORY memory_1 (
    .DR__LD(DR__LD), .R(R), .T1(T1), .D7(D7), .I(I), .T3(T3), .T4(T4), .D3(D3), .D5(D5), .T6(T6), .D6(D6),
    .READ(Memory__READ), .WRITE(Memory__WRITE));
  PC pc_1 (
    .T4(T4), .D4(D4), .T5(T5), .D5(D5), .T1(T1), .R(R), .T2(T2), .D6(D6), .T6(T6), .DR(DR), .AC(ACC),
    .B2(IR[2]), .B4(IR[4]), .r_2(r_t), .B3(IR[3]), .B1(IR[1]), .E(E), .p(p), .B9(IR[9]), .FGI(FGI),
    .B8(IR[8]), .FGO(FGO), .LD(PC__LD), .CLR(PC__CLR), .INR(PC__INR));
  and and_12 (AND, T5, D0);
  and and_13 (ADD, T5, D1);
  and and_14 (DR_PASS, D2, T5);
endmodule

module AR (
  input  T0,
  input  T2,
  input  R,
  input  T3,
  input  D7,
  input  I,
  input  T4,
  input  D5,
  output LD,
  output INR,
  output CLR
);

  wire and_1_out, and_2_out, not_1_out, not_2_out, or_1_out;

  or or_1 (or_1_out, T0, T2);
  not not_1 (not_1_out, R);
  not not_2 (not_2_out, D7);
  and and_1 (and_1_out, or_1_out, not_1_out);
  and and_2 (and_2_out, T3, not_2_out, I);
  and and_3 (INR, T4, D5);
  and and_4 (CLR, R, T0);
  or or_2 (LD, and_1_out, and_2_out);
endmodule

module ACC (
  input  T5,
  input  D0,
  input  D1,
  input  D2,
  input  r,
  input  B6,
  input  B7,
  input  B9,
  input  B11,
  input  p,
  input  B5,
  output LD,
  output INR,
  output CLR
);

  wire and_1_out, and_2_out, and_3_out, or_1_out, or_2_out;

  or or_1 (or_1_out, D0, D1, D2);
  or or_2 (or_2_out, B6, B7, B9, B5);
  and and_1 (and_1_out, T5, or_1_out);
  and and_2 (and_2_out, r, or_2_out);
  and and_3 (and_3_out, B11, p);
  and and_4 (INR, r, B5);
  and and_5 (CLR, r, B11);
  or or_3 (LD, and_1_out, and_2_out, and_3_out);
endmodule

module PC (
  input  T4,
  input  D4,
  input  T5,
  input  D5,
  input  T1,
  input  R,
  input  T2,
  input  D6,
  input  T6,
  input  [15:0] DR,
  input  [15:0] AC,
  input  B2,
  input  B4,
  input  r_2,
  input  B3,
  input  B1,
  input  E,
  input  p,
  input  B9,
  input  FGI,
  input  B8,
  input  FGO,
  output LD,
  output CLR,
  output INR
);

  wire and_1_out, and_2_out, and_4_out, and_5_out, and_6_out, and_7_out, and_8_out, and_9_out, and_10_out,
       and_11_out, and_12_out, not_1_out, not_2_out, not_3_out, not_4_out, not_5_out, or_2_out, or_3_out;

  and and_1 (and_1_out, T4, D4);
  and and_2 (and_2_out, T5, D5);
  not not_1 (not_1_out, R);
  not not_2 (not_2_out, E);
  or or_1 (LD, and_1_out, and_2_out);
  and and_3 (CLR, T1, R);
  and and_4 (and_4_out, T1, not_1_out);
  and and_5 (and_5_out, R, T2);
  not not_3 (not_3_out, AC[15]);
  and and_6 (and_6_out, not_3_out, B4, r_2);
  and and_7 (and_7_out, AC[15], r_2, B3);
  and and_8 (and_8_out, r_2, B1, not_2_out);
  and and_9 (and_9_out, p, B9, FGI);
  and and_10 (and_10_out, p, B8, FGO);
  not not_4 (not_4_out, or_2_out);
  or or_2 (or_2_out, DR[0], DR[1], DR[2], DR[3], DR[4], DR[5], DR[6], DR[7], DR[8], DR[9], DR[10], DR[11], DR[12], DR[13], DR[14], DR[15]);
  or or_3 (or_3_out, AC[0], AC[1], AC[2], AC[3], AC[4], AC[5], AC[6], AC[7], AC[8], AC[9], AC[10], AC[11], AC[12], AC[13], AC[14], AC[15]);
  not not_5 (not_5_out, or_3_out);
  and and_11 (and_11_out, D6, T6, not_4_out);
  and and_12 (and_12_out, not_5_out, B2, r_2);
  or or_4 (INR, and_4_out, and_5_out, and_11_out, and_12_out, and_6_out, and_7_out, and_8_out, and_9_out, and_10_out);
endmodule

module DR (
  input  T4,
  input  D0,
  input  D1,
  input  D2,
  input  D6,
  input  T5,
  output LD,
  output INR
);

  wire or_1_out;

  and and_1 (LD, T4, or_1_out);
  or or_1 (or_1_out, D0, D1, D2, D6);
  and and_2 (INR, D6, T5);
endmodule

module OUTR (
  input  p,
  input  B10,
  output LD
);

  and and_1 (LD, p, B10);
endmodule

module IR (
  input  R,
  input  T1,
  output LD
);

  wire not_1_out;

  not not_1 (not_1_out, R);
  and and_1 (LD, not_1_out, T1);
endmodule

module TR (
  input  R,
  input  T0,
  output LD
);

  and and_1 (LD, R, T0);
endmodule

module R (
  input  T0,
  input  T1,
  input  T2,
  input  IEN,
  input  FGI,
  input  FGO,
  input  R,
  input  T3,
  output SET,
  output RESET
);

  wire not_1_out, not_2_out, not_3_out, or_1_out;

  not not_1 (not_1_out, T0);
  not not_2 (not_2_out, T1);
  not not_3 (not_3_out, T2);
  or or_1 (or_1_out, FGI, FGO);
  and and_1 (RESET, R, T3);
  and and_2 (SET, not_1_out, not_2_out, not_3_out, IEN, or_1_out);
endmodule

module IEN (
  input  B7,
  input  p,
  input  B6,
  input  R,
  input  T2,
  output SET,
  output RESET
);

  wire and_2_out, and_3_out;

  and and_1 (SET, B7, p);
  and and_2 (and_2_out, p, B6);
  and and_3 (and_3_out, R, T2);
  or or_1 (RESET, and_2_out, and_3_out);
endmodule

module FGI (
  input  p,
  input  B11,
  output RESET
);

  and and_1 (RESET, p, B11);
endmodule

module FGO (
  input  p,
  input  B10,
  input  T0,
  output RESET,
  output SET
);

  and and_1 (RESET, p, B10);

  assign SET = T0;
endmodule

module I (
  input  R,
  input  T2,
  input  IR_15,
  output SET,
  output RESET
);

  wire not_1_out, not_2_out;

  not not_1 (not_1_out, R);
  not not_2 (not_2_out, IR_15);
  and and_1 (SET, not_1_out, T2, IR_15);
  and and_2 (RESET, not_1_out, not_2_out, T2);
endmodule

module E (
  input  r,
  input  B6,
  input  B7,
  input  B8,
  input  B10,
  output SET,
  output RESET
);

  wire or_1_out;

  or or_1 (or_1_out, B6, B7, B8);
  and and_1 (RESET, r, B10);
  and and_2 (SET, r, or_1_out);
endmodule

module SC (
  input  T3,
  input  R,
  input  T5,
  input  D3,
  input  D4,
  input  T6,
  input  D0,
  input  D1,
  input  D2,
  input  D5,
  input  T7,
  input  D6,
  input  r_NEW,
  input  p_NEW,
  output CLR
);

  wire and_1_out, and_2_out, and_3_out, and_4_out, or_1_out, or_2_out;

  and and_1 (and_1_out, T3, R);
  or or_1 (or_1_out, D3, D4);
  or or_2 (or_2_out, D0, D1, D2, D5);
  and and_2 (and_2_out, T5, or_1_out);
  and and_3 (and_3_out, T6, or_2_out);
  and and_4 (and_4_out, T7, D6);
  or or_3 (CLR, and_1_out, and_2_out, and_3_out, and_4_out, r_NEW, p_NEW);
endmodule

module S (
  input  r,
  input  B0,
  output RESET
);

  and and_1 (RESET, r, B0);
endmodule

module MEMORY (
  input  DR__LD,
  input  R,
  input  T1,
  input  D7,
  input  I,
  input  T3,
  input  T4,
  input  D3,
  input  D5,
  input  T6,
  input  D6,
  output READ,
  output WRITE
);

  wire and_1_out, and_2_out, and_3_out, and_4_out, and_5_out, not_1_out, not_2_out, or_1_out;

  not not_1 (not_1_out, R);
  and and_1 (and_1_out, not_1_out, T1);
  not not_2 (not_2_out, D7);
  and and_2 (and_2_out, not_2_out, I, T3);
  or or_1 (or_1_out, D3, D5);
  or or_2 (READ, DR__LD, and_1_out, and_2_out);
  and and_3 (and_3_out, T4, or_1_out);
  and and_4 (and_4_out, R, T1);
  and and_5 (and_5_out, T6, D6);
  or or_3 (WRITE, and_3_out, and_4_out, and_5_out);
endmodule

module BUS_CONTROL (
  input  T4,
  input  D4,
  input  T5,
  input  D5,
  input  T0,
  input  D6,
  input  T6,
  input  D3,
  input  p,
  input  B10,
  input  R,
  input  T2,
  input  T1,
  input  MEMORY__READ,
  output S0,
  output S1,
  output S2
);

  wire and_1_out, and_2_out, and_3_out, and_7_out, and_8_out, not_1_out, X1, X2, X3, X4, X5, X6;

  and and_1 (and_1_out, T4, D3);
  and and_2 (and_2_out, p, B10);
  not not_1 (not_1_out, R);
  and and_3 (and_3_out, D5, T4);
  or or_1 (X2, and_3_out, T0);
  and and_4 (X3, D6, T6);
  or or_2 (X4, and_1_out, and_2_out);
  and and_5 (X5, not_1_out, T2);
  and and_6 (X6, R, T1);
  and and_7 (and_7_out, T4, D4);
  or or_3 (X1, and_7_out, and_8_out);
  and and_8 (and_8_out, T5, D5);
  or or_4 (S0, X1, X3, X5, MEMORY__READ);
  or or_5 (S1, X2, X3, X6, MEMORY__READ);
  or or_6 (S2, X4, X5, X6, MEMORY__READ);

  // Other names for the same wires on the sheet: X7 = MEMORY__READ
endmodule

module DELAY (
  input  INP,
  output DELAY
);

  wire and_1_out, d_ff_1_qn, not_1_out;

  and and_1 (and_1_out, INP, not_1_out);
  not not_1 (not_1_out, INP);
  D_Flip_Flop d_ff_1 (.clk(and_1_out), .D(d_ff_1_qn), .Q(DELAY), .Qn(d_ff_1_qn));  // open: preset, en, reset
endmodule
